# Fritzing sketch electronics_rev3 (saved by Fritzing 0.9.3b)
circuit board: 2.37975cm x 2.38cm
circuit board: 1.96661cm x 1.61383cm
circuit board: 3.4cm x 3.4cm
circuit board: 2.95856cm x 1.44211cm
circuit board: 6.93686cm x 6.39485cm
circuit board: 1.8596cm x 1.29661cm
breadboards: 1

parts:
  EMFD = Rectifier Diode [part_number=1N4001 package="300 mil [THT]"]
  0_1uF = Electrolytic Capacitor [capacitance=10nF package="100 mil [THT, electrolytic]"]
  100R = Resistor [tolerance=±5% resistance=220 package=THT]
  J1 = male pin header, 3 pins [form="♂ (male)"]
  BATTERY_PACK_~11v = Battery block 9V  # not connected
  UBEC1 = Mystery Part - 4 pins [package=THT]  # not connected
  DIV_1_6KR = 220 Ω Resistor [package=THT]
  DIV_2_3KR = 220 Ω Resistor [package=THT]
  R10K = Resistor [tolerance=±5% resistance=10k package=THT]
  R10K_2 = Resistor [tolerance=±5% resistance=10k package=THT]
  FR = Basic FET N-Channel [package="TO220 [THT]"]
  FB = Basic FET P-Channel [package="TO220 [THT]"]
  SR = Basic FET P-Channel [package="TO220 [THT]"]
  SG = Basic FET P-Channel [package="TO220 [THT]"]
  SB = Basic FET P-Channel [package="TO220 [THT]"]
  IR = Basic FET P-Channel [package="TO220 [THT]"]
  T1 = LM35 Temperature Sensor [package="TO92 [THT]"]
  12VDC_-_+ = screw terminal, 4 pins
  TRG2 = female pin header, 2 pins [form="♀ (female)"]
  +_Shoot = female pin header, 5 pins [form="♀ (female)"]
  Laser = female pin header, 2 pins [form="♀ (female)"]
  +_Flash = female pin header, 4 pins [form="♀ (female)"]
  S_+_- = female pin header, 3 pins [form="♀ (female)"]
  TRG1 = female pin header, 2 pins [form="♀ (female)"]
  SHOOT = female pin header, 5 pins [form="♀ (female)"]
  IR_1_5R = Resistor [tolerance=±5% resistance=220 package=THT]
  RB = Resistor [tolerance=±5% resistance=220 package=THT]
  RG = Resistor [tolerance=±5% resistance=220 package=THT]
  RR = Resistor [tolerance=±5% resistance=220 package=THT]
  LED3 = LED - 5mm [color="Infrared (940nm)" package="5 mm [THT]"]
  RB_2 = Resistor [tolerance=±5% resistance=220 package=THT]
  RR_2 = Resistor [tolerance=±5% resistance=220 package=THT]
  RG_2 = Resistor [tolerance=±5% resistance=220 package=THT]
  FLASH = female pin header, 4 pins [form="♀ (female)"]
  J3 = male pin header, 3 pins [form="♂ (male)"]
  J4 = male pin header, 3 pins [form="♂ (male)"]
  J5 = male pin header, 3 pins [form="♂ (male)"]
  J6 = male pin header, 3 pins [form="♂ (male)"]
  J7 = male pin header, 3 pins [form="♂ (male)"]
  J8 = male pin header, 3 pins [form="♂ (male)"]
  J9 = male pin header, 3 pins [form="♂ (male)"]
  J10 = male pin header, 3 pins [form="♂ (male)"]
  J11 = male pin header, 3 pins [form="♂ (male)"]
  S2_+_- = female pin header, 3 pins [form="♀ (female)"]
  KEY = female pin header, 2 pins [form="♀ (female)"]
  0_1uF1 = Electrolytic Capacitor [capacitance=10nF package="100 mil [THT, electrolytic]"]
  100R2 = Resistor [tolerance=±5% resistance=220 package=THT]
  J12 = male pin header, 3 pins [form="♂ (male)"]
  U5 = IC, SIP package, 4 pins [chip_label=IC]
  U6 = IC, SIP package, 4 pins [chip_label=IC]
  U7 = IC, SIP package, 4 pins [chip_label=IC]
  Raspberry_Pi_1 = Raspberry Pi 3 [part_number=RPI-3-V1.2]
  5V_(0R)_GND = Resistor [tolerance=±5% resistance=0 package=THT]
  AUX1 = female pin header, 3 pins [form="♀ (female)"]
  ATMEGA328 = atmega328 [package=dip]
  C2 = Ceramic Capacitor [capacitance="100 nF" package="100 mil [THT, multilayer]"]
  C1 = Ceramic Capacitor [capacitance="100 nF" package="100 mil [THT, multilayer]"]
  XTAL = Crystal [frequency="16 Mhz" package=THT]
  AUX2 = female pin header, 3 pins [form="♀ (female)"]
  U9 = IC, SIP package, 4 pins [chip_label=IC]
  J13 = female pin header, 1 pin [form="♀ (female)"]
  J14 = female pin header, 1 pin [form="♀ (female)"]
  10uF = Capacitor Polarized [package=cpol-radial-10uf-25v]
  10uF_2 = Capacitor Polarized [package=cpol-radial-10uf-25v]
  REG = Voltage Regulator - Variable [package="TO220 [THT]"]
  Coil_+ = male pin header, 1 pin [form="♂ (male)"]
  Relay_IN = male pin header, 1 pin [form="♂ (male)"]
  Coil_- = male pin header, 1 pin [form="♂ (male)"]
  Relay_OUT = male pin header, 1 pin [form="♂ (male)"]
  nc = male pin header, 1 pin [form="♂ (male)"]  # not connected
  RCBG = RGB LED (com. anode, rbg) [package="5 mm [THT]"]
  RCBG1 = RGB LED (com. anode, rbg) [package="5 mm [THT]"]
  FG = Basic FET N-Channel [package="TO220 [THT]"]

nets:
  N1: EMFD.cathode, Raspberry_Pi_1.GIPO16, ATMEGA328.D10_(PWM), Coil_+.pin1
  GND: EMFD.anode, DIV_2_3KR.Pin_1, R10K.Pin_1, R10K_2.Pin_1, FR.source, FB.source, SR.source, SG.source, SB.source, IR.source, 12VDC_-_+.pin2, 12VDC_-_+.pin4, Laser.pin2, S_+_-.pin3, S2_+_-.pin3, Raspberry_Pi_1.GND, 5V_(0R)_GND.Pin_1, AUX1.pin1, ATMEGA328.GND, C2.0, C1.0, AUX2.pin1, 10uF.-, 10uF_2.-, REG.ADJ, Coil_-.pin1, FG.source
  N2: 0_1uF.-, J1.pin3, T1.GND
  N3: 0_1uF.+, 100R.Pin_1, T1.Vout
  N4: 100R.Pin_0, J1.pin2
  N5: J1.pin1, T1.+Vs
  N6: DIV_1_6KR.Pin_0, KEY.pin2, 10uF.+, REG.IN, Relay_OUT.pin1
  N7: DIV_1_6KR.Pin_1, DIV_2_3KR.Pin_0, ATMEGA328.A0
  N8: R10K.Pin_0, TRG1.pin2, ATMEGA328.D3_(PWM)
  N9: R10K_2.Pin_0, TRG2.pin2, ATMEGA328.D2
  N10: FR.gate, Raspberry_Pi_1.GIPO23, ATMEGA328.D11_(PWM)
  N11: FR.drain, +_Flash.pin4
  N12: FB.gate, Raspberry_Pi_1.GIPO24, ATMEGA328.D13
  N13: FB.drain, +_Flash.pin2
  N14: SR.gate, ATMEGA328.D4
  N15: SR.drain, +_Shoot.pin5
  N16: SG.gate, ATMEGA328.D5_(PWM)
  N17: SG.drain, +_Shoot.pin4
  N18: SB.gate, ATMEGA328.D6_(PWM)
  N19: SB.drain, +_Shoot.pin3
  N20: IR.gate, ATMEGA328.D9_(PWM)
  N21: IR.drain, +_Shoot.pin2
  N22: 12VDC_-_+.pin1, 12VDC_-_+.pin3, KEY.pin1, Relay_IN.pin1
  5V: TRG2.pin1, +_Shoot.pin1, +_Flash.pin1, S_+_-.pin2, TRG1.pin1, S2_+_-.pin2, Raspberry_Pi_1.5V, 5V_(0R)_GND.Pin_0, AUX1.pin3, ATMEGA328.VCC, ATMEGA328.AVCC, AUX2.pin3, 10uF_2.+, REG.OUT
  N23: Laser.pin1, ATMEGA328.D7
  N24: +_Flash.pin3, FG.drain
  N25: S_+_-.pin1, ATMEGA328.D8
  N26: SHOOT.pin1, LED3.anode, RCBG1.common_anode
  N27: SHOOT.pin2, IR_1_5R.Pin_0
  N28: SHOOT.pin3, RB.Pin_1
  N29: SHOOT.pin4, RG.Pin_1
  N30: SHOOT.pin5, RR.Pin_1
  N31: IR_1_5R.Pin_1, LED3.cathode
  N32: RB.Pin_0, RCBG1.blue_cathode
  N33: RG.Pin_0, RCBG1.green_cathode
  N34: RR.Pin_0, RCBG1.red_cathode
  N35: RB_2.Pin_0, RCBG.blue_cathode
  N36: RB_2.Pin_1, FLASH.pin2
  N37: RR_2.Pin_0, RCBG.red_cathode
  N38: RR_2.Pin_1, FLASH.pin4
  N39: RG_2.Pin_0, RCBG.green_cathode
  N40: RG_2.Pin_1, FLASH.pin3
  N41: FLASH.pin1, RCBG.common_anode
  N42: J3.pin1, J4.pin1, J5.pin1, J6.pin1, J7.pin1, J8.pin1, J9.pin1, J10.pin1, J11.pin1
  N43: J3.pin2, J4.pin2, J5.pin2, J6.pin2, J7.pin2, J8.pin2, J9.pin2, J10.pin2, J11.pin2
  N44: J3.pin3, J4.pin3, J5.pin3, J6.pin3, J7.pin3, J8.pin3, J9.pin3, J10.pin3, J11.pin3
  N45: S2_+_-.pin1, ATMEGA328.A1
  N46: 0_1uF1.-, J12.pin3, U5.pin1, U6.pin1, U7.pin1, U9.pin1
  N47: 0_1uF1.+, 100R2.Pin_1, U5.pin2, U6.pin2, U7.pin2, U9.pin2
  N48: 100R2.Pin_0, J12.pin2
  N49: J12.pin1, U5.pin3, U5.pin4, U6.pin3, U6.pin4, U7.pin3, U7.pin4, U9.pin3, U9.pin4
  N50: Raspberry_Pi_1.GIPO12, ATMEGA328.RESET
  N51: Raspberry_Pi_1.GIPO18, ATMEGA328.D12, FG.gate
  N52: Raspberry_Pi_1.GIPO15, ATMEGA328.D1_(TX)
  N53: Raspberry_Pi_1.GIPO14, ATMEGA328.D0_(RX)
  N54: AUX1.pin2, ATMEGA328.A2
  N55: ATMEGA328.XLAT1, C2.1, XTAL.pin_0
  N56: ATMEGA328.XLAT2, C1.1, XTAL.pin_1
  N57: ATMEGA328.A3, AUX2.pin2
  N58: ATMEGA328.A4, J14.pin1
  N59: ATMEGA328.A5, J13.pin1

notes:
  Battery Monitoring Voltage divider
  Sensor PCB
  This line links arduino and battery grounds
  S + -
  VCC
  Tag Mainboard Rev 3

custom parts:
  Mystery Part - 4 pins: A dummy, proxy, ersatz, stand-in part for whatever you want. With 4 pins on a 100 mil inline pin header footprint.
  220 Ω Resistor: A generic resistor (0.25W)
  220 Ω Resistor: A generic resistor (0.25W)

// code stored in the sketch: IRcomms.ino
//The IR communication components.
//
// Hacked together by Andrew Shirley

// Code which was either 'copypasta'ed or used as inspiration at some point:
//
// http://www.arduino.cc/cgi-bin/yabb2/YaBB.pl?num=1240843250 Copyright (C) Timo Herva aka 'mettapera', 2009
// http://tthheessiiss.wordpress.com/2009/08/05/dirt-cheap-wireless/ 

//NB. as these are quite time intensive enabling this often breaks it :-(
//#define DEBUG_SEND 1
//#define DEBUG_RECV 1

// pin numbers (9 is used for a Carrier wave and so isn't available)
#define pin_infrared 8 // ir LED
#define pin_ir_feedback 13 // normal LED
#define pin_ir_reciever_port PINB  // These 2 equate to pin 12
#define pin_ir_reciever_bit 4      // "           "          "
#define pin_ir_reciever 12         // normal LED

// some timings
long headerDuration = 2400;
long intervalDuration = 600;
long oneDuration = 1200;
long zeroDuration = 600;

byte timingTolerance = 100;

////////////////////////
// IR Writing variables
unsigned long writeBuffer = 0;
byte writeBits = 0;
unsigned long writeUpTime = 0;
unsigned long writeDownTime = 0;
unsigned long writeLastChangeTime = 0;

////////////////////////
// IR reading variables
unsigned long readBuffer = 0;
byte bitsRead = 0;

byte oldPinValue = 0;

//the micros for the point at which the IR went high
unsigned long readRiseTime = 0;

//the micros for the point at which the IR went low
unsigned long readFallTime = 0;

////////////////////////
// IR reading functions

//read the IR receiver and if applicable add to the readBuffer. This will return 1 if the transmission appears to be complete. Subsequent reads will return 0.
int signal_recieve() {
  byte pinValue = ! bitRead(pin_ir_reciever_port, pin_ir_reciever_bit);

  if (!oldPinValue && pinValue) {
    //IR rising edge
    readRiseTime = micros();
    oldPinValue = HIGH;
#ifdef DEBUG_RECV
    Serial.print("\\ @");
    Serial.println(readRiseTime);
#endif
    //there is always more to be read if the IR is high.
    return 0;
  }
  else if (oldPinValue && !pinValue) {
    //IR falling edge
    readFallTime = micros();
    unsigned long duration = readFallTime - readRiseTime;

    if (within_tolerance(duration, headerDuration, timingTolerance)) {
      //we are within tolerance of 2400 us - a restart
      readBuffer = 0;
      bitsRead = 0;
#ifdef DEBUG_RECV
      Serial.println("--");
#endif
    }
    else if (within_tolerance(duration, oneDuration, timingTolerance)) {
      //we are within tolerance of 1200 us - a one
      readBuffer = (readBuffer << 1) + 1;
      bitsRead++;
#ifdef DEBUG_RECV
      Serial.println("-1");
#endif
    }
    else if (within_tolerance(duration, zeroDuration, timingTolerance)) {
      //we are within tolerance of 600 us - a zero
      readBuffer = readBuffer << 1;
      bitsRead++;
#ifdef DEBUG_RECV
      Serial.println("-0");
#endif
    }
    else {
#ifdef DEBUG_RECV
      Serial.print("/ @");
      Serial.print(readFallTime);
      Serial.print("  ");
      Serial.println(duration);
#endif
    }

    oldPinValue = LOW;
    //wait to see if there is more to be read
    return 0;
  }
  else if (oldPinValue) {
    //IR continues to be high
    //there is always more to be read if the IR is high.
    return 0;
  }
  else /*if (!oldPinValue)*/ {
    //IR continues to be low
    //if we have been low for more than interval + tolerance (twice for extra leniency) we can assume the transmission has finished and try to read it.
    if (!readFallTime) {
      //we aren't waiting for an interval, all quiet on the IR front.
      return 0;
    }
    else if (micros() - readFallTime > intervalDuration + timingTolerance * 2) {
      readFallTime = 0; //cache this result
#ifdef DEBUG_RECV
      Serial.println("xx");
#endif
      return 1;
    }
    else {
      //still low, waiting for the interval
      return 0;
    }
  }
}

boolean within_tolerance(unsigned long value, unsigned long target, byte tolerance) {
  long remainder = value - target;
  return remainder < tolerance && remainder > -tolerance;
}

////////////////////////
// IR writing functions

void start_command(unsigned long command) {
  if (writeUpTime || writeDownTime) {
    //already writing - this is an error
    //Serial.println("tried to start a command when we are already sending");
    return;
  }

  command = reverse(command, 16);
  writeBuffer = addParityBit(command);
  writeBits = 17;

  //write header
  ir_up();
#ifdef DEBUG_SEND
  Serial.println("  \\");
#endif
  writeDownTime = headerDuration;
}

void signal_send() {
  unsigned long elapsed = micros() - writeLastChangeTime;
  
  if (writeDownTime && writeDownTime <= elapsed) {
#ifdef DEBUG_SEND
    Serial.print("  /");
    Serial.print(elapsed);
    Serial.print(" - ");
    Serial.println(writeDownTime, DEC);
#endif
    ir_down();
    writeDownTime = 0;
    
    if (writeBits) {
      //not done yet
      writeUpTime = intervalDuration;
    }
  }
  else if (writeUpTime && writeUpTime <= elapsed) {
#ifdef DEBUG_SEND
    Serial.print("  \\");
    Serial.print(elapsed);
    Serial.print(" - ");
    Serial.println(writeUpTime, DEC);
#endif
    ir_up();
    writeUpTime = 0;
    
    if (writeBuffer & B1) {
      //write a one
      writeDownTime = oneDuration;
    }
    else {
      //write a zero
      writeDownTime = zeroDuration;
    }
    
    writeBuffer = writeBuffer >> 1;
    writeBits--;
  }
}

void ir_up() {
  digitalWrite(pin_infrared, HIGH);
  digitalWrite(pin_ir_feedback, HIGH);
  writeLastChangeTime = micros();
}

void ir_down() {
  digitalWrite(pin_infrared, LOW);
  digitalWrite(pin_ir_feedback, LOW);
  writeLastChangeTime = micros();
}

/*
 * Reverse the num least significant bits.
 */
unsigned long reverse(unsigned long in, int num) {
  unsigned long out = 0;
  for (int i = 0; i < num; i++) {
    out = out << 1;
    out = out | (in & 1); //take the lsb from in to out
    in = in >> 1;
  }
  
  return out;
}

unsigned long timeCache = 0;

void timeDebug() {
  if (timeCache == 0) {
    timeCache = micros();
  }
  else {
    Serial.println(micros() - timeCache);
    timeCache = 0;
  }
}

// code stored in the sketch: main.ino
//#define DEBUG_DECODE 1

void decode_signal() {
#ifdef DEBUG_DECODE
  Serial.print("==");
  Serial.println(readBuffer, BIN);
  Serial.println(readBuffer, HEX);
#endif
}

//setting things ready
void setup() {
  //set the pins
  pinMode(pin_infrared, OUTPUT);
  pinMode(9, OUTPUT);
  pinMode(pin_ir_feedback, OUTPUT);
  pinMode(pin_ir_reciever, INPUT);
  
  // see http://www.atmel.com/dyn/resources/prod_documents/doc8161.pdf for more details (page 136 onwards)
  //set the carrier wave frequency. This only sets up pin 9.
  TCCR1A = _BV(COM1A0); // | _BV(COM1B0); for another pin (10)
  TCCR1B = _BV(WGM12) | _BV(CS10);
  
  TIMSK1 = 0; //no interupts
  TIFR1 = _BV(OCF1A) | _BV(OCF1A); //clear Output Compare Match Flags (by setting them :-P )
  unsigned long desired_freq = 40000;
  OCR1A = 10000000/desired_freq - 1; // see page 126 of datasheet for this equation
  //OCR1B = 10000000/desired_freq - 1; for another pin (10)

  ir_down();

  //debug  
  Serial.begin(9600);
}


unsigned long time = micros();

void loop() {
  if (micros() > time + 1000000) {
    time = micros();
    mt_fireShot();
  }

  signal_send();
  if (signal_recieve()) {
    decode_signal();
    mt_parseIRMessage(readBuffer);
  }
}

// code stored in the sketch: miles_tag_defines.ino

#define SYSTEM_MESSAGE                      B000

#define SYSTEM_MESSAGE_MASK                 0x1f00 // i.e. 5 least significant bits of the most significant byte
#define SYSTEM_MESSAGE_SHIFT                8

#define SYSTEM_MESSAGE_ADD_HEALTH           B00001
#define SYSTEM_MESSAGE_ADD_ROUNDS           B00010
#define SYSTEM_MESSAGE_ADD_CLIPS            B00011
#define SYSTEM_MESSAGE_ADD_RPG_ROUNDS       B00100

#define SYSTEM_MESSAGE_GOD_GUN              B01001

#define SYSTEM_MESSAGE_SCORE_DATA_HEADER    B10000
#define SYSTEM_MESSAGE_SCORE_REQUEST        B10001

#define SYSTEM_MESSAGE_SET_TEAM_ID          B10110
#define SYSTEM_MESSAGE_SET_PLAYER_ID        B10111

#define GOD_GUN_KILL_PLAYER                 0x00
#define GOD_GUN_PAUSE_PLAYER                0x01

#define GOD_GUN_START_GAME                  0x03
#define GOD_GUN_RESPAWN_PLAYER              0x04
#define GOD_GUN_INIT_PLAYER                 0x05
#define GOD_GUN_FULL_AMMO                   0x06
#define GOD_GUN_END_PLAYER                  0x07

#define UNLIMITED_CLIPS                     255
#define UNLIMITED_AMMO                      255


#define MT1_TEAM_MASK                       0xe000 // i.e. 3 most significant bits
#define MT1_TEAM_OFFSET                     13 // i.e. 3 most significant bits
#define MT1_PLAYER_MASK                     0x1f00 // i.e. 5 least significant bits of the most significant byte
#define MT1_PLAYER_OFFSET                   8 // i.e. 5 least significant bits of the most significant byte

#define MT1_DAMAGE_RESURRECT_OPPONENT       -1

// code stored in the sketch: miles_tag_gun_logic.ino
//milestag protocol 1 documented at http://www.lasertagparts.com/mtformat.htm
//milestag protocol 2 documented at http://www.lasertagparts.com/mtformat-2.htm
// we currently only implement MT1 as MT2 seems incomplete.

void serialPrint(int size, const char * fmt, ...) {
  char* out = (char*) malloc(size);
  va_list ap;
  va_start(ap, fmt);
  
  vsnprintf(out, size, fmt, ap);
  Serial.println(out);
  free(out);
  
  va_end (ap);
}

void mt_parseIRMessage(unsigned long recvBuffer) {
    if (!isEvenParity(recvBuffer)) {
        serialPrint(14, "Shot(Corrupt)");
        return;
    }

    //trim the 17th bit (parity) off to make things neater
    recvBuffer = recvBuffer >> 1;

    byte recv_TeamID = (recvBuffer & MT1_TEAM_MASK) >> MT1_TEAM_OFFSET;
    byte DataByte2 = recvBuffer & 0xff;

    if (recv_TeamID == SYSTEM_MESSAGE) {
        byte recv_SystemMessage = (recvBuffer & SYSTEM_MESSAGE_MASK) >> SYSTEM_MESSAGE_SHIFT;
        
        switch (recv_SystemMessage) {
            case SYSTEM_MESSAGE_SET_TEAM_ID:
                serialPrint(19, "Shot(SetTeam(%u))", DataByte2);
                break;
            case SYSTEM_MESSAGE_SET_PLAYER_ID:
                serialPrint(21, "Shot(SetPlayer(%u))", DataByte2);
                break;
            case SYSTEM_MESSAGE_ADD_HEALTH:
                serialPrint(21, "Shot(AddHealth(%u))", DataByte2);
                break;
            case SYSTEM_MESSAGE_ADD_CLIPS:
            {
                serialPrint(20, "Shot(AddClips(%u))", DataByte2);
                break;
            }
            case SYSTEM_MESSAGE_GOD_GUN:
            {
                byte recv_GodGun = DataByte2;
                switch (recv_GodGun) {
                    case GOD_GUN_KILL_PLAYER:
                        serialPrint(15, "Shot(Killed())");
                        break;
                    case GOD_GUN_FULL_AMMO:
                        serialPrint(17, "Shot(FullAmmo())");
                        break;
                    case GOD_GUN_RESPAWN_PLAYER:
                        serialPrint(15, "Shot(ReSpawn())");
                        break;
                    case GOD_GUN_PAUSE_PLAYER:
                    case GOD_GUN_START_GAME:
                    case GOD_GUN_INIT_PLAYER:
                    case GOD_GUN_END_PLAYER:
                    default:
                        serialPrint(17, "Shot(UnknownGGM)");
                        break;
                }
                
                break;
            }
            case SYSTEM_MESSAGE_ADD_ROUNDS:
                serialPrint(21, "Shot(AddRounds(%u))", DataByte2);
                break;
            case SYSTEM_MESSAGE_ADD_RPG_ROUNDS:
            case SYSTEM_MESSAGE_SCORE_DATA_HEADER:
            case SYSTEM_MESSAGE_SCORE_REQUEST:
            default:
                serialPrint(28, "Shot(UnknownSM(%lu))", recvBuffer);
                break;
        }
    } else {
        byte recv_PlayerID = (recvBuffer & MT1_PLAYER_MASK) >> MT1_PLAYER_OFFSET;
        signed char damage;
        
        byte recv_PlayerWeaponHit = DataByte2;
        switch (recv_PlayerWeaponHit) {
            case 0:
            {
                damage = MT1_DAMAGE_RESURRECT_OPPONENT;
                break;
            }
            case 1 ... 100:
            {
                damage = recv_PlayerWeaponHit;
                break;
            }
            //No 'Base' Mode
            /*case 101 ... 200:
            {
                recv_PlayerWeaponHit -= 100;
                baseDamage = recv_PlayerWeaponHit;
            }
            case 255:
                baseDamage = MT1_DAMAGE_RESURRECT_ENEMY_BASE;
            */

            default:
                serialPrint(17, "Shot(UnknownDmg)");
                break;
        }
        
        serialPrint(23, "Shot(Hit(%u,%u,%u))", recv_PlayerID, recv_TeamID, damage/*, baseDamage*/);
    }
}


void mt_fireShot() {
//  unsigned long shot = (TeamID << MT1_TEAM_OFFSET) | (PlayerID << MT1_PLAYER_OFFSET) | GunDamage;
  unsigned long shot = (0x01l << MT1_TEAM_OFFSET) | (0x01l << MT1_PLAYER_OFFSET) | 0x03l;

  //serialPrint(20, "shot: %ul", shot);

  start_command(shot);
}

// code stored in the sketch: parity.ino

boolean isEvenParity(unsigned long buf) {
  boolean evenParityBit = false;
  for (int i = 0; i < sizeof(unsigned long) * 8; i++) {
    evenParityBit = evenParityBit ^ (buf & 1);
    buf = buf >> 1;
  }
  return !evenParityBit;
}

unsigned long addParityBit(unsigned long in) {
  if (!isEvenParity(in)) {
    return in | 0x00010000;
  }
  else {
    return in;
  }
}
